# Fritzing sketch CalculatorSchematic (saved by Fritzing 0.9.2b)
breadboards: 5

parts:
  LCD1 = LCD screen
  R1 = Trimmer Potentiometer [maximum_resistance=10kΩ package=THT]
  Part1 = Arduino Uno (Rev3)
  R2 = Resistor [tolerance=±5% resistance=330 package="0603 [SMD]"]
  S1 = Pushbutton [package="[THT]"]
  S2 = Pushbutton [package="[THT]"]
  S3 = Pushbutton [package="[THT]"]
  S4 = Pushbutton [package="[THT]"]
  S5 = Pushbutton [package="[THT]"]
  S6 = Pushbutton [package="[THT]"]
  S7 = Pushbutton [package="[THT]"]
  S8 = Pushbutton [package="[THT]"]
  S9 = Pushbutton [package="[THT]"]
  S10 = Pushbutton [package="[THT]"]
  S11 = Pushbutton [package="[THT]"]
  S12 = Pushbutton [package="[THT]"]
  S13 = Pushbutton [package="[THT]"]
  S14 = Pushbutton [package="[THT]"]
  S15 = Pushbutton [package="[THT]"]
  S16 = Pushbutton [package="[THT]"]
  S17 = Pushbutton [package="[THT]"]
  S18 = Pushbutton [package="[THT]"]
  S20 = Pushbutton [package="[THT]"]
  S21 = Pushbutton [package="[THT]"]
  S22 = Pushbutton [package="[THT]"]
  S23 = Pushbutton [package="[THT]"]
  S19 = Pushbutton [package="[SMD]"]

nets:
  N1: LCD1.R/W, LCD1.LED-, R1.leg1, Part1.GND
  N2: LCD1.E, Part1.D11_PWM/MOSI
  N3: LCD1.DB4, Part1.D5_PWM
  N4: LCD1.DB5, Part1.D4
  N5: LCD1.DB6, Part1.D3_PWM
  N6: LCD1.DB7, Part1.D2
  N7: R1.leg2, Part1.5V, R2.Pin_1
  N8: Part1.A0, S1.Pin_1, S1.Pin_2, S2.Pin_1, S2.Pin_2, S3.Pin_1, S3.Pin_2, S4.Pin_1, S4.Pin_2, S5.Pin_1, S5.Pin_2, S6.Pin_1, S6.Pin_2
  N9: S1.Pin_3, S1.Pin_4
  N10: S2.Pin_3, S2.Pin_4
  N11: S3.Pin_3, S3.Pin_4
  N12: S4.Pin_3, S4.Pin_4
  N13: S5.Pin_3, S5.Pin_4
  N14: S6.Pin_3, S6.Pin_4
  N15: S7.Pin_1, S7.Pin_2, S8.Pin_1, S8.Pin_2, S9.Pin_1, S9.Pin_2, S10.Pin_1, S10.Pin_2, S11.Pin_1, S11.Pin_2, S12.Pin_1, S12.Pin_2, S13.Pin_1, S13.Pin_2
  N16: S7.Pin_3, S7.Pin_4
  N17: S8.Pin_3, S8.Pin_4
  N18: S9.Pin_3, S9.Pin_4
  N19: S10.Pin_3, S10.Pin_4
  N20: S11.Pin_3, S11.Pin_4
  N21: S12.Pin_3, S12.Pin_4
  N22: S13.Pin_3, S13.Pin_4
  N23: S14.Pin_1, S14.Pin_2, S15.Pin_1, S15.Pin_2, S16.Pin_1, S16.Pin_2, S17.Pin_1, S17.Pin_2, S18.Pin_1, S18.Pin_2, S19.Pin_1, S19.Pin_2
  N24: S14.Pin_3, S14.Pin_4
  N25: S15.Pin_3, S15.Pin_4
  N26: S16.Pin_3, S16.Pin_4
  N27: S17.Pin_3, S17.Pin_4
  N28: S18.Pin_3, S18.Pin_4
  N29: S20.Pin_1, S20.Pin_2, S21.Pin_1, S21.Pin_2, S22.Pin_1, S22.Pin_2, S23.Pin_1, S23.Pin_2
  N30: S20.Pin_3, S20.Pin_4
  N31: S21.Pin_3, S21.Pin_4
  N32: S22.Pin_3, S22.Pin_4
  N33: S23.Pin_3, S23.Pin_4
  N34: S19.Pin_3, S19.Pin_4
